# Fritzing sketch altitude_sensor (saved by Fritzing 0.9.3b)
breadboards: 1

parts:
  Part1 = Adafruit VL53L0X Time of Flight Distance Sensor [part_number="Adafruit #3317"]
  Part2 = Adafruit_BMP280
  SONAR1 = Maxbotix MaxSonar Ultrasonic Sensor (Hi-Res)
  Teensy_3_1 = Teensy 3.1

nets:
  VIN: Part1.VIN, Part2.VIN, SONAR1.+5V, Teensy_3_1.3V3
  GND: Part1.GND, Part2.GND, SONAR1.GND, Teensy_3_1.GND
  N1: Part1.SCL, Part2.SCK/SCL, Teensy_3_1.A5/D19
  N2: Part1.SDA, Part2.SDI/SDA, Teensy_3_1.A4/D18
  N3: SONAR1.AN, Teensy_3_1.A0/D14

custom parts:
  Adafruit VL53L0X Time of Flight Distance Sensor: The VL53L0X is a Time of Flight distance sensor like no other you've used! The sensor contains a very tiny invisible laser source, and a matching sensor. The VL53L0X can detect the "time of flight", or how long the light has taken to bounce back to the sensor. Since it uses a very narrow light source, it is good for determining distance of only the surface directly in front of it. Unlike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
  Adafruit_BMP280: Bosch has stepped up their game with their new BMP280 sensor, an environmental sensor with temperature, barometric pressure that is the next generation upgrade to the BMP085/BMP180/BMP183. This sensor is great for all sorts of weather sensing and can even be used in both I2C and SPI! This precision sensor from Bosch is the best low-cost, precision sensing solution for measuring barometric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
  Maxbotix MaxSonar Ultrasonic Sensor (Hi-Res): Maxbotix MaxSonar Hi-Resolution Ultrasonic Sensor HRLV-EZ0, HRLV-EZ1, HRLV-EZ2, HRLV-EZ3, HRLV-EZ4
